# Fritzing sketch SERVO_POTE (saved by Fritzing 0.9.3b)

parts:
  J1 = Basic Servo  # not connected
  Componente1 = Arduino Uno (Rev3)
  U1 = POT [package=pot_mammoth]

nets:
  N1: Componente1.A0, U1.A
  N2: Componente1.3V3, U1.S
  N3: Componente1.GND, U1.E

notes:
  Al girar el potenciómetro el eje del servo rota
